# Fritzing sketch Circuit (saved by Fritzing 0.9.3b)
breadboards: 2

parts:
  F2 = Fan - Ventilador [package=THT]
  U5 = Module 4 Relais 5V [package="Module 4 Relais 5V"]
  PIR2 = PIR sensor
  S6 = Momentary Switch [package=ksa_sealed_tac_switch]
  S7 = Momentary Switch [package=ksa_sealed_tac_switch]
  S8 = Momentary Switch [package=ksa_sealed_tac_switch]
  S9 = Momentary Switch [package=ksa_sealed_tac_switch]
  BULB2 = Incandescent light bulb small [package="bulb sm"]
  R3 = Resistor [tolerance=±5% resistance=220 package="0402 [SMD]"]
  R4 = Resistor [tolerance=±5% resistance=220 package="0402 [SMD]"]
  U7 = NodeMCU V1.0
  SG4 = Buzzer 12mm [part_number=COM-07950 package=buzzer-12mm-ns]
  Linh_kiện2 = MQ-3 breakout
  DHT11_1 = DHT11 module
  R5 = Resistor [tolerance=±5% resistance=220 package="0402 [SMD]"]
  R6 = Resistor [tolerance=±5% resistance=220 package="0402 [SMD]"]
  OLED_I2C1 = OLED 128x64 I2C Monochrome Display
  OLED_I2C2 = OLED 128x64 I2C Monochrome Display
  DHT11_2 = DHT11 module
  F3 = Fan - Ventilador [package=THT]
  BULB3 = Incandescent light bulb small [package="bulb sm"]
  U9 = LuaNode32 / ESP32 [part_number=ESP32S-PIN30]
  F4 = Fan - Ventilador [package=THT]
  U10 = Module 4 Relais 5V [package="Module 4 Relais 5V"]
  BULB4 = Incandescent light bulb small [package="bulb sm"]
  F5 = Fan - Ventilador [package=THT]  # not connected
  F6 = Fan - Ventilador [package=THT]  # not connected
  F7 = Fan - Ventilador [package=THT]  # not connected
  U11 = Module 4 Relais 5V [package="Module 4 Relais 5V"]  # not connected
  U12 = Module 4 Relais 5V [package="Module 4 Relais 5V"]  # not connected
  PIR3 = PIR sensor
  S10 = Momentary Switch [package=ksa_sealed_tac_switch]  # not connected
  S11 = Momentary Switch [package=ksa_sealed_tac_switch]  # not connected
  S12 = Momentary Switch [package=ksa_sealed_tac_switch]
  S13 = Momentary Switch [package=ksa_sealed_tac_switch]
  BULB5 = Incandescent light bulb small [package="bulb sm"]  # not connected
  BULB6 = Incandescent light bulb small [package="bulb sm"]  # not connected
  BULB7 = Incandescent light bulb small [package="bulb sm"]  # not connected
  R7 = Resistor [tolerance=±5% resistance=220 package="0402 [SMD]"]  # not connected
  R8 = Resistor [tolerance=±5% resistance=220 package="0402 [SMD]"]  # not connected
  R9 = Resistor [tolerance=±5% resistance=220 package="0402 [SMD]"]  # not connected
  R10 = Resistor [tolerance=±5% resistance=220 package="0402 [SMD]"]  # not connected
  U13 = NodeMCU V1.0
  SG5 = Buzzer 12mm [part_number=COM-07950 package=buzzer-12mm-ns]
  Linh_kiện3 = MQ-3 breakout  # not connected
  DHT11_3 = DHT11 module
  OLED_I2C3 = OLED 128x64 I2C Monochrome Display
  OLED_I2C4 = OLED 128x64 I2C Monochrome Display  # not connected
  DHT11_4 = DHT11 module  # not connected
  U14 = LuaNode32 / ESP32 [part_number=ESP32S-PIN30]  # not connected

nets:
  VCC: F2.5V, U5.VCC, PIR2.VDD, BULB2.1, R3.Pin_0, R4.Pin_0, U7.Vin, Linh_kiện2.VCC, DHT11_1.VCC, R5.Pin_1, R6.Pin_1, OLED_I2C1.VDD, OLED_I2C2.VDD, DHT11_2.VCC, F3.5V, BULB3.1, U9.Vin, F4.5V, U10.VCC, BULB4.1
  N1: F2.GND, U5.K1-NO
  GND: U5.GND, PIR2.GND, S6.4, S8.4, S9.2, U7.GND, SG4.2, Linh_kiện2.GND, DHT11_1.GND, OLED_I2C1.GND, OLED_I2C2.GND, DHT11_2.GND, U9.GND, U10.GND, U10.K1-NF, U10.K3-NF
  N2: U5.IN1, U9.D14
  N3: U5.IN2, U9.D27
  N4: U5.IN3, U9.D26
  N5: U5.IN4, U9.D25
  N6: U5.K1-NF, U5.K2-NF, U5.K3-NF, U5.K4-NF
  N7: U5.K2-NO, BULB2.2
  N8: U5.K3-NO, F3.GND
  N9: U5.K4-NO, BULB3.2
  N10: PIR2.SIG, U7.D5
  N11: S6.1, R5.Pin_0
  N12: S6.2, U7.D3
  N13: S6.3, S7.1
  N14: S7.3, R6.Pin_0
  N15: S7.4, U7.D0
  N16: S8.2, R4.Pin_1, U9.D15
  N17: S9.4, R3.Pin_1, U9.D2
  N18: U7.D1, OLED_I2C1.SCK
  N19: U7.D2, OLED_I2C1.SDA
  N20: U7.D4, DHT11_1.DATA
  N21: U7.D6, SG4.1
  N22: U7.A0, Linh_kiện2.AO
  N23: OLED_I2C2.SDA, U9.D21
  N24: OLED_I2C2.SCK, U9.D22
  N25: DHT11_2.DATA, U9.D32
  N26: U9.D34, U10.IN3
  N27: U9.D35, U10.IN1
  N28: F4.GND, U10.K1-NO
  N29: U10.K3-NO, BULB4.2
  N30: PIR3.SIG, U13.D5
  N31: S12.1, U13.D0
  N32: S13.1, U13.D3
  N33: U13.D1, OLED_I2C3.SCK
  N34: U13.D2, OLED_I2C3.SDA
  N35: U13.D4, DHT11_3.DATA
  N36: U13.D6, SG5.1

notes:
  Relay 4 kênh 5v
  ESP32 WROOM 32
  ESP8266 NodeMCU
  MQ2 - PIR - DHT11
  OLED 128x64 0.96 inch

custom parts:
  Fan - Ventilador: Ventilador de 2 pines, se encuentra comunmente en computadoras de escritorio
  Module 4 Relais 5V: Module 4 Relais 5V 4x SPD-06VDC-SD-C
  NodeMCU V1.0: ESP8266 based NodeMCU
  Buzzer 12mm: Buzzer 12mm Spark Fun Electronics SKU : Comp-Buzzer Through hole This is a small 12mm round speaker that operates around the audible 2kHz range. You can use these speakers to create simple music or user interfaces. This is not a true piezoelectric speaker but behaves similarly. Instead of a piezoelectric crystal that vibrates with an electric current, this tiny speaker uses an electromagnet to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
  MQ-3 breakout: Alcohol sensor is capable of detecting alcohol (ethanol) particles on itself and gives the information in digital form back to us to manipulate with it. SKU:101251 • Voltage: 5V DC • Power: max 750mW • Measurement range: 0.04-4mg/L
  DHT11 module: https://cdn-learn.adafruit.com/downloads/pdf/dht.pdf DHT11 black pcb module reference by:https://github.com/adafruit/Fritzing-Library/blob/master/parts/DHT11%20Humitidy%20and%20Temperature%20Sensor.fzpz
  LuaNode32 / ESP32: New Image for LuaNode32 DOIT ESP32 DEVKIT V1. Base parts from LuaNode32 / ESP32 ESP32 based LuaNode32 by G.Noorlander DOIT Esp32 DevKit v1 (30 pins long, 11 pins width) by Werner Rothschopf (modified by vanepp Dec 2018)
