# Fritzing sketch Circuit (saved by Fritzing 0.9.3b)
breadboards: 2

parts:
  S6 = Momentary Switch [package=ksa_sealed_tac_switch]
  S7 = Momentary Switch [package=ksa_sealed_tac_switch]
  U7 = NodeMCU V1.0
  DHT11_1 = DHT11 module
  R5 = Resistor [tolerance=±5% resistance=220 package="0402 [SMD]"]
  R6 = Resistor [tolerance=±5% resistance=220 package="0402 [SMD]"]
  OLED_I2C1 = OLED 128x64 I2C Monochrome Display
  F4 = Fan - Ventilador [package=THT]
  U10 = Module 4 Relais 5V [package="Module 4 Relais 5V"]
  BULB4 = Incandescent light bulb small [package="bulb sm"]

nets:
  N1: S6.1, R5.Pin_0
  N2: S6.2, U7.D3
  N3: S6.3, S7.1
  GND: S6.4, U7.GND, DHT11_1.GND, OLED_I2C1.GND, U10.GND, U10.K1-NF, U10.K2-NF
  N4: S7.3, R6.Pin_0
  N5: S7.4, U7.D0
  N6: U7.D1, OLED_I2C1.SCK
  N7: U7.D2, OLED_I2C1.SDA
  N8: U7.D4, DHT11_1.DATA
  N9: U7.D6, U10.IN1
  N10: U7.D7, U10.IN3
  VCC: U7.Vin, DHT11_1.VCC, R5.Pin_1, R6.Pin_1, OLED_I2C1.VDD, F4.5V, U10.VCC, BULB4.1
  N11: F4.GND, U10.K2-NO
  N12: U10.K1-NO, BULB4.2

notes:
  Relay 4 kênh 5v
  ESP8266 NodeMCU
  OLED 128x64 0.96 inch
  DHT11

custom parts:
  NodeMCU V1.0: ESP8266 based NodeMCU
  DHT11 module: https://cdn-learn.adafruit.com/downloads/pdf/dht.pdf DHT11 black pcb module reference by:https://github.com/adafruit/Fritzing-Library/blob/master/parts/DHT11%20Humitidy%20and%20Temperature%20Sensor.fzpz
  Fan - Ventilador: Ventilador de 2 pines, se encuentra comunmente en computadoras de escritorio
  Module 4 Relais 5V: Module 4 Relais 5V 4x SPD-06VDC-SD-C
